# Fritzing sketch Load_Ballancer (saved by Fritzing 0.9.3b)
breadboards: 1

parts:
  BAT3 = Battery Holders [package=battery-aa]
  Q1 = TRANSISTOR_NPN [package=to-92-ammo]
  Q2 = PNP-Transistor [package="TO92 [THT]"]
  R1 = Resistor [tolerance=±5% resistance=220 package=THT]
  10K = Resistor [tolerance=±5% resistance=220 package=THT]
  BAT4 = Battery Holders [package=battery-aa]
  R3 = Resistor [tolerance=±5% resistance=220 package=THT]
  R4 = Resistor [tolerance=±5% resistance=220 package=THT]
  LOAD_BALANCER_NPN = Header 1 [package=1x01_offset]
  LOAD_BALANCER_PNP = Header 1 [package=1x01_offset]
  D1 = SOLAR-IXYS [package=solarbit-12x1]
  10K1 = Resistor [tolerance=±5% resistance=220 package=THT]
  GND = Header 1 [package=1x01_offset]
  SOLARZELLE = Header 1 [package=1x01_offset]
  VCC = Header 1 [package=1x01_offset]

nets:
  N1: BAT3.-, Q2.E, VCC.1
  N2: BAT3.+, R1.Pin_1, BAT4.-, R3.Pin_0
  N3: Q1.E, BAT4.+
  N4: Q1.B, 10K.Pin_1
  N5: Q1.C, R1.Pin_0
  N6: Q2.B, R4.Pin_0
  N7: Q2.C, R3.Pin_1
  N8: 10K.Pin_0, LOAD_BALANCER_NPN.1
  N9: R4.Pin_1, LOAD_BALANCER_PNP.1
  N10: D1.A, 10K1.Pin_0, GND.1
  N11: D1.C, 10K1.Pin_1, SOLARZELLE.1

notes:
  Basiswiderstand:
  10K
  Kollektorwiderstand:
  1K
