# Fritzing sketch arduino_display_18b20 (saved by Fritzing 0.9.6b)
breadboards: 1

parts:
  U1 = atmega328 [package=dip]
  Bauteil1 = NRF24L01+ Breakout Board
  S1 = Pushbutton [package="[THT]"]
  R1 = Resistor [tolerance=±5% resistance=22k power=0.25 package=THT]
  Nokia_5110_LCD_Module1 = Nokia 5110 LCD
  DS1 = DS18B20 1-Wire Temperature Sensor [part_number=DS18B20]

nets:
  N1: U1.RESET, S1.Pin_1, S1.Pin_2, R1.Pin_1
  N2: U1.D2, Nokia_5110_LCD_Module1.RST
  N3: U1.D3_(PWM), Nokia_5110_LCD_Module1.BL
  N4: U1.D4, Nokia_5110_LCD_Module1.CE
  VCC: U1.VCC, U1.AVCC, U1.AREF, Bauteil1.VCC, R1.Pin_0, Nokia_5110_LCD_Module1.VCC, DS1.VDD
  GND: U1.GND, Bauteil1.GND, S1.Pin_3, S1.Pin_4, Nokia_5110_LCD_Module1.GND, DS1.GND
  N5: U1.D5_(PWM), Nokia_5110_LCD_Module1.D/C
  N6: U1.D6_(PWM), Nokia_5110_LCD_Module1.Din
  N7: U1.D7, Nokia_5110_LCD_Module1.CLK
  N8: U1.D8, DS1.DQ
  N9: U1.D9_(PWM), Bauteil1.CS
  N10: U1.D10_(PWM), Bauteil1.CE
  N11: U1.D11_(PWM), Bauteil1.MOSI
  N12: U1.D12, Bauteil1.MISO
  N13: U1.D13, Bauteil1.SCK

custom parts:
  Nokia 5110 LCD: Nokia 5110 Graphic 84*48 LCD module <Blue Version>
