# Fritzing sketch arduino_minimal (saved by Fritzing 0.9.6b)
breadboards: 1

parts:
  U1 = atmega328 [package=dip]
  Bauteil1 = NRF24L01+ Breakout Board
  S1 = Pushbutton [package="[THT]"]
  R1 = Resistor [tolerance=±5% resistance=22k power=0.25 package=THT]

nets:
  N1: U1.RESET, S1.Pin_1, S1.Pin_2, R1.Pin_1
  VCC: U1.VCC, U1.AVCC, U1.AREF, Bauteil1.VCC, R1.Pin_0
  GND: U1.GND, Bauteil1.GND, S1.Pin_3, S1.Pin_4
  N2: U1.D9_(PWM), Bauteil1.CS
  N3: U1.D10_(PWM), Bauteil1.CE
  N4: U1.D11_(PWM), Bauteil1.MOSI
  N5: U1.D12, Bauteil1.MISO
  N6: U1.D13, Bauteil1.SCK
